# Fritzing sketch Example-1_Wireless (saved by Fritzing 0.9.9b)
breadboards: 1

parts:
  part = ESP8266-01S [part_number=ESP-01S-Breakout]  # not connected
  part_2 = ESP8266-01S [part_number=ESP-01S-Breakout]  # not connected
  part_3 = ESP8266-01S [part_number=ESP-01S-Breakout]  # not connected
  part_4 = ESP8266-01S [part_number=ESP-01S-Breakout]  # not connected
  U1 = ESP8266-01S [part_number=ESP-01S-Breakout]
  part_5 = ESP8266-01S [part_number=ESP-01S-Breakout]  # not connected
  U2 = ESP8266-01S [part_number=ESP8266]
  Part1 = Arduino Uno (Rev3)

nets:
  N1: U1.RXD#0, Part1.D12/MISO
  N2: U1.VCC#1, U1.CH_PD#5, Part1.3V3
  N3: U1.GND#6, Part1.GND
  N4: U1.TXD#7, Part1.D13/SCK
  N5: U1.RXD#8, U2.RXD
  N6: U1.VCC#9, U2.VCC
  N7: U1.GPIO_0#10, U2.GPIO_0
  N8: U1.RST#11, U2.RST
  N9: U1.GPIO_2#12, U2.GPIO_2
  N10: U1.CH_PD#13, U2.CH_PD
  N11: U1.GND#14, U2.GND
  N12: U1.TXD#15, U2.TXD
