# Fritzing sketch ESP-01-Joystick (saved by Fritzing 0.9.9b)
breadboards: 1

parts:
  U1 = ESP8266-01S [part_number=ESP-01S-Breakout]
  U2 = ESP8266-01S [part_number=ESP8266]
  Part1 = Arduino Uno (Rev3)
  S2 = Pushbutton [package="[THT]"]
  S3 = Pushbutton [package="[THT]"]

nets:
  N1: U1.RXD#0, Part1.D0/RX
  N2: U1.VCC#1, U1.CH_PD#5, Part1.3V3
  N3: U1.GPIO_0#2, S2.Pin_1, S2.Pin_2
  N4: U1.RST#3, S3.Pin_1, S3.Pin_2
  N5: U1.GND#6, Part1.RESET, Part1.GND, S2.Pin_3, S2.Pin_4, S3.Pin_3, S3.Pin_4
  N6: U1.TXD#7, Part1.D1/TX
  N7: U1.RXD#8, U2.RXD
  N8: U1.VCC#9, U2.VCC
  N9: U1.GPIO_0#10, U2.GPIO_0
  N10: U1.RST#11, U2.RST
  N11: U1.GPIO_2#12, U2.GPIO_2
  N12: U1.CH_PD#13, U2.CH_PD
  N13: U1.GND#14, U2.GND
  N14: U1.TXD#15, U2.TXD
