# Fritzing sketch Example-1_Motor-Driving (saved by Fritzing 0.9.9b)
breadboards: 1

parts:
  Part1 = Arduino Uno (Rev3)
  IC1 = L293D [package=THT]
  M2 = ChinaMotor
  U1 = POT [package=pot_alpha_rv16af-20]
  S1 = Pushbutton [package="[THT]"]
  R1 = Resistor [tolerance=±1% resistance=10000 package=THT]

nets:
  N1: Part1.A0, U1.S
  N2: Part1.D11_PWM/MOSI, IC1.Enable_1
  N3: Part1.D12/MISO, S1.Pin_1, S1.Pin_2, R1.Pin_1
  N4: Part1.D6_PWM, IC1.In_2
  N5: Part1.D7, IC1.In_1
  N6: Part1.5V, IC1.+Vmotor, IC1.+V, U1.A, S1.Pin_3, S1.Pin_4
  N7: Part1.GND, IC1.0V, U1.E, R1.Pin_0
  N8: IC1.Out_1_(_Controlled_by_Enable_1_), M2.pin_2
  N9: IC1.Out_2_(_Controlled_by_Enable_1_), M2.pin_1

custom parts:
  ChinaMotor: Your standard DC Motor
