# Fritzing sketch Tiny-Breadboard-Putting-it-All-Together (saved by Fritzing 0.9.9b)
breadboards: 1

parts:
  U1 = ESP8266-01S [part_number=ESP-01S-Breakout]
  U2 = ESP8266-01S [part_number=ESP8266]
  Part1 = Arduino Uno (Rev3)
  IC1 = L293D [package=THT]
  VCC1 = 4 x AA Battery Mount
  M1 = ChinaMotor
  M2 = ChinaMotor
  VCC2 = Battery block 9V  # not connected

nets:
  N1: U1.RXD#0, Part1.D12/MISO
  N2: U1.VCC#1, U1.CH_PD#5, Part1.3V3
  N3: U1.GND#6, Part1.GND, IC1.0V, VCC1.-
  N4: U1.TXD#7, Part1.D13/SCK
  N5: U1.RXD#8, U2.RXD
  N6: U1.VCC#9, U2.VCC
  N7: U1.GPIO_0#10, U2.GPIO_0
  N8: U1.RST#11, U2.RST
  N9: U1.GPIO_2#12, U2.GPIO_2
  N10: U1.CH_PD#13, U2.CH_PD
  N11: U1.GND#14, U2.GND
  N12: U1.TXD#15, U2.TXD
  N13: Part1.D10_PWM/SS, IC1.Enable_2
  N14: Part1.D11_PWM/MOSI, IC1.Enable_1
  N15: Part1.D4, IC1.In_3
  N16: Part1.D5_PWM, IC1.In_4
  N17: Part1.D6_PWM, IC1.In_2
  N18: Part1.D7, IC1.In_1
  N19: Part1.5V, IC1.+V
  N20: IC1.Out_1_(_Controlled_by_Enable_1_), M1.pin_2
  N21: IC1.Out_2_(_Controlled_by_Enable_1_), M1.pin_1
  N22: IC1.+Vmotor, VCC1.+
  N23: IC1.Out_3_(_Controlled_by_Enable_2_), M2.pin_2
  N24: IC1.Out_4_(_Controlled_by_Enable_2_), M2.pin_1

custom parts:
  ChinaMotor: Your standard DC Motor
